// Digital circuit MUX.dig as structural Verilog
module MUX (
  input  D,
  input  C,
  input  B,
  input  A,
  output Y
);

  wire not_1_out;
  wire [2:1] undriven;

  not not_1 (not_1_out, D);
  Multiplexer #(.Selector_Bits(3)) multiplexer_1 (
    .sel({undriven, A}), .in_0(D), .in_1(D), .in_2(D), .in_3(D), .in_4(not_1_out), .in_5(not_1_out),
    .in_6(not_1_out), .in_7(1'b0), .out(Y));

  assign B = A;
  assign C = A;
  // also tied to VCC on the sheet: D

  // Notes on the sheet:
  //   Use A as the most-significant bit and 
  //   D as the least-significant bit.
  //   Converts between single bits & a 3-bit bus
endmodule

/* Test case:
A B C D Y
0 0 0 0 X
0 0 0 1 1
*/
