// Digital circuit SOP.dig as structural Verilog
module SOP (
  input  A,
  input  D,
  output Y
);

  wire and_1_out, and_2_out, not_1_out, not_2_out;

  not not_1 (not_1_out, A);
  not not_2 (not_2_out, D);
  and and_1 (and_1_out, A, not_2_out, not_2_out);  // open: In_2
  and and_2 (and_2_out, not_1_out, D);  // open: In_1, In_4
  or or_1 (Y, and_1_out, and_2_out);  // open: In_1, In_4

  // Notes on the sheet:
  //   A: MSB
  //   D: LSB
  //   Use A as the most-significant bit and 
  //   D as the least-significant bit.
endmodule

/* Test case:
A B C D Y
0 0 0 0 X
0 0 0 1 1
*/
